# Fritzing sketch Binky093 (saved by Fritzing 0.9.3b)
breadboards: 1

parts:
  R1 = Resistor [tolerance=±5% resistance=220 package=THT]
  J1 = screw terminal, 9 pins
  D1 = Rectifier Diode [part_number=1N4001 package="300 mil [THT]"]
  F1 = Resettable Fuse PTC [part_number=pfra50 package=ptc]
  LED1 = LED - 3mm [color="Red (633nm)" package="3 mm [THT]"]
  R2 = Resistor [tolerance=±5% resistance=220 package=THT]
  LED2 = LED - 3mm [color="Red (633nm)" package="3 mm [THT]"]
  D2 = Rectifier Diode [part_number=1N4001 package="300 mil [THT]"]
  F2 = Resettable Fuse PTC [part_number=pfra50 package=ptc]
  R3 = Resistor [tolerance=±5% resistance=220 package=THT]
  LED3 = LED - 3mm [color="Red (633nm)" package="3 mm [THT]"]
  D3 = Rectifier Diode [part_number=1N4001 package="300 mil [THT]"]
  F3 = Resettable Fuse PTC [part_number=pfra50 package=ptc]
  R4 = Resistor [tolerance=±5% resistance=220 package=THT]
  LED4 = LED - 3mm [color="Red (633nm)" package="3 mm [THT]"]
  D4 = Rectifier Diode [part_number=1N4001 package="300 mil [THT]"]
  F4 = Resettable Fuse PTC [part_number=pfra50 package=ptc]
  R5 = Resistor [tolerance=±5% resistance=220 package=THT]
  LED5 = LED - 3mm [color="Red (633nm)" package="3 mm [THT]"]
  D5 = Rectifier Diode [part_number=1N4001 package="300 mil [THT]"]
  F5 = Resettable Fuse PTC [part_number=pfra50 package=ptc]
  R6 = Resistor [tolerance=±5% resistance=220 package=THT]
  LED6 = LED - 3mm [color="Red (633nm)" package="3 mm [THT]"]
  D6 = Rectifier Diode [part_number=1N4001 package="300 mil [THT]"]
  F6 = Resettable Fuse PTC [part_number=pfra50 package=ptc]
  R7 = Resistor [tolerance=±5% resistance=220 package=THT]
  LED7 = LED - 3mm [color="Red (633nm)" package="3 mm [THT]"]
  D7 = Rectifier Diode [part_number=1N4001 package="300 mil [THT]"]
  F7 = Resettable Fuse PTC [part_number=pfra50 package=ptc]
  R8 = Resistor [tolerance=±5% resistance=220 package=THT]
  LED8 = LED - 3mm [color="Red (633nm)" package="3 mm [THT]"]
  D8 = Rectifier Diode [part_number=1N4001 package="300 mil [THT]"]
  F8 = Resettable Fuse PTC [part_number=pfra50 package=ptc]

nets:
  N1: R1.Pin_0, J1.pin2, F1.1
  N2: R1.Pin_1, LED1.anode
  N3: J1.pin1, R3.Pin_0, F3.1
  N4: J1.pin3, R2.Pin_0, F2.1
  N5: J1.pin4, R4.Pin_0, F4.1
  N6: J1.pin5, R5.Pin_0, F5.1
  N7: J1.pin6, R6.Pin_0, F6.1
  N8: J1.pin7, R7.Pin_0, F7.1
  N9: J1.pin8, R8.Pin_0, F8.1
  N10: D1.cathode, F1.2
  N11: D1.anode, LED1.cathode
  N12: R2.Pin_1, LED2.anode
  N13: LED2.cathode, D2.anode
  N14: D2.cathode, F2.2
  N15: R3.Pin_1, LED3.anode
  N16: LED3.cathode, D3.anode
  N17: D3.cathode, F3.2
  N18: R4.Pin_1, LED4.anode
  N19: LED4.cathode, D4.anode
  N20: D4.cathode, F4.2
  N21: R5.Pin_1, LED5.anode
  N22: LED5.cathode, D5.anode
  N23: D5.cathode, F5.2
  N24: R6.Pin_1, LED6.anode
  N25: LED6.cathode, D6.anode
  N26: D6.cathode, F6.2
  N27: R7.Pin_1, LED7.anode
  N28: LED7.cathode, D7.anode
  N29: D7.cathode, F7.2
  N30: R8.Pin_1, LED8.anode
  N31: LED8.cathode, D8.anode
  N32: D8.cathode, F8.2
