# Fritzing sketch BinkyDCC-Ext (saved by Fritzing 0.9.3b)
circuit board: 8.5cm x 6cm
breadboards: 1

parts:
  R3 = Resistor [tolerance=±5% resistance=10k package=THT]
  R1 = Resistor [tolerance=±5% resistance=1k package=THT]
  Q1 = NPN-Transistor [part_number=BC547 package="TO92 [THT]"]
  R2 = Resistor [tolerance=±5% resistance=1k package=THT]
  J3LCD = female pin header, 4 pins [form="♀ (female)"]
  R4 = Rotary Potentiometer (Small) [maximum_resistance=10kΩ package=THT]
  Part1 = Arduino Pro Mini (5V)
  J1HBR = female pin header, 8 pins [form="♀ (female)"]
  J1 = Generic double row female header - 26 pins [form="♀ (female)" package=THT]
  J2 = Screw terminal - 2 pins [package=THT]

nets:
  CURB: R3.Pin_0, Part1.A0, J1HBR.pin5, J1HBR.pin6
  GND: R3.Pin_1, Q1.E, J3LCD.pin1, R4.leg1, Part1.GND, J1HBR.pin8, J1.GND, J2.pin1
  5V: R1.Pin_0, J3LCD.pin2, R4.leg2, Part1.VCC, J1HBR.pin7, J1.5V, J2.pin2
  N1: R1.Pin_1, Q1.C, J1HBR.pin2
  N2: Q1.B, R2.Pin_1
  PWM: R2.Pin_0, J1HBR.pin1, J1.UART1_TX/PG06
  SDA: J3LCD.pin3, Part1.A4
  SCL: J3LCD.pin4, Part1.A5
  MAXC: R4.wiper, Part1.A1
  ENREQ: Part1.D5, J1.UART2_TX/PA00
  EN: Part1.D3, J1HBR.pin3, J1HBR.pin4, J1.UART2_RA/PA01

notes:
  ArduinoBooster
  5V GND

custom parts:
  Generic double row female header - 26 pins: Generic double row female header
