# Fritzing sketch BinkyDCC (saved by Fritzing 0.9.3b)
breadboards: 1

parts:
  R3 = Resistor [tolerance=±5% resistance=10k package=THT]
  R1 = Resistor [tolerance=±5% resistance=1k package=THT]
  U1 = ATTINY13 [package=dip]
  Q1 = NPN-Transistor [part_number=BC547 package="TO92 [THT]"]
  R2 = Resistor [tolerance=±5% resistance=1k package=THT]
  J3LCD = female pin header, 4 pins [form="♀ (female)"]
  J2OPI = female pin header, 4 pins [form="♀ (female)"]
  R4 = Rotary Potentiometer (Small) [maximum_resistance=10kΩ package=THT]
  J1HBR = double row female pin header, 8 pins [form="♀ (female)"]
  R5 = Resistor [tolerance=±5% resistance=10k package=THT]

nets:
  CURB: R3.Pin_0, U1.PB3(ADC3), J1HBR.pin5, J1HBR.pin6
  GND: R3.Pin_1, U1.GND, Q1.E, J3LCD.pin1, J2OPI.pin2, R4.leg1, J1HBR.pin8
  5V: R1.Pin_0, U1.VCC, J3LCD.pin2, J2OPI.pin1, R4.leg2, J1HBR.pin7, R5.Pin_1
  N1: R1.Pin_1, Q1.C, J1HBR.pin2
  N2: U1.PB5(NRES), R5.Pin_0
  MAXC: U1.PB4(ADC2), R4.wiper
  SDA: U1.PB0(MOSI), J3LCD.pin3
  EN: U1.PB1(MISO), J2OPI.pin4, J1HBR.pin3, J1HBR.pin4
  SCL: U1.PB2(SCK_ADC1), J3LCD.pin4
  N3: Q1.B, R2.Pin_1
  PWM: R2.Pin_0, J2OPI.pin3, J1HBR.pin1

notes:
  1=5V, 2=GND, 3=PWM, 4=EN
  ArduinoBooster
