# Fritzing sketch BinkyNetIO.old (saved by Fritzing 0.9.3b)
breadboards: 1

parts:
  U1 = RELAY-2 [package=relay-g5v]
  IC1 = MCP23017 I2C I/O Expander
  IC2 = P82B715PN [chip_label=IC package="DIP (Dual Inline) [THT]"]
  Q1 = HT7333 [part_number=HT7333 package=sot89]
  C1 = Ceramic Capacitor [capacitance=100nF package="100 mil [THT, multilayer]"]
  R1 = Resistor [tolerance=±5% resistance=220 package=THT]
  R2 = Resistor [tolerance=±5% resistance=220 package=THT]
  D1 = Rectifier Diode [part_number=1N4001 package="300 mil [THT]"]
  U2 = RELAY-2 [package=relay-g5v]
  D2 = Rectifier Diode [part_number=1N4001 package="300 mil [THT]"]
  U3 = RELAY-2 [package=relay-g5v]
  D3 = Rectifier Diode [part_number=1N4001 package="300 mil [THT]"]
  U4 = RELAY-2 [package=relay-g5v]
  D4 = Rectifier Diode [part_number=1N4001 package="300 mil [THT]"]
  U5 = RELAY-2 [package=relay-g5v]
  D5 = Rectifier Diode [part_number=1N4001 package="300 mil [THT]"]
  U6 = RELAY-2 [package=relay-g5v]
  D6 = Rectifier Diode [part_number=1N4001 package="300 mil [THT]"]
  U7 = RELAY-2 [package=relay-g5v]
  D7 = Rectifier Diode [part_number=1N4001 package="300 mil [THT]"]
  U8 = RELAY-2 [package=relay-g5v]
  D8 = Rectifier Diode [part_number=1N4001 package="300 mil [THT]"]
  J1 = female pin header, 10 pins [form="♀ (female)"]
  R3 = Resistor [tolerance=±5% resistance=220 package=THT]

nets:
  5V: U1.2, IC1.VDD, Q1.Vin, D1.cathode, U2.2, D2.cathode, U3.2, D3.cathode, U4.2, D4.cathode, U5.2, D5.cathode, U6.2, D6.cathode, U7.2, D7.cathode, U8.2, D8.cathode, J1.pin1, R3.Pin_1
  RIO0: U1.9, IC1.GPB0, D1.anode
  RIO1: IC1.GPB1, U2.9, D2.anode
  RIO2: IC1.GPB2, U3.9, D3.anode
  RIO3: IC1.GPB3, U4.9, D4.anode
  RIO4: IC1.GPB4, U5.9, D5.anode
  RIO5: IC1.GPB5, U6.9, D6.anode
  RIO6: IC1.GPB6, U7.9, D7.anode
  RIO7: IC1.GPB7, U8.9, D8.anode
  GND: IC1.VSS, IC2.pin4, Q1.GND, C1.0, J1.pin2
  SCL: IC1.SCL, IC2.pin3, R2.Pin_1
  SDA: IC1.SDA, IC2.pin6, R1.Pin_1
  N1: IC1.RESET, R3.Pin_0
  GIO0: IC1.GPA0, J1.pin3
  GIO1: IC1.GPA1, J1.pin4
  GIO2: IC1.GPA2, J1.pin5
  GIO3: IC1.GPA3, J1.pin6
  GIO4: IC1.GPA4, J1.pin7
  GIO5: IC1.GPA5, J1.pin8
  GIO6: IC1.GPA6, J1.pin9
  GIO7: IC1.GPA7, J1.pin10
  SCLB: IC2.pin2
  SDAB: IC2.pin7
  3.3V: IC2.pin8, Q1.Vout
  N2: C1.1, R1.Pin_0, R2.Pin_0

custom parts:
  MCP23017 I2C I/O Expander: The MCP23017 uses two i2c pins (these can be shared with other i2c devices), and in exchange gives you 16 general purpose pins. You can set each of 16 pins to be input, output, input with a pullup or open drain. There's even the ability to get an interrupt via an external pin when any of the inputs change so you don't have to keep polling the chip.
  P82B715PN: I2C-bus extender
  HT7333: 3v3 regulator
