# Fritzing sketch BinkyNetIOSmall (saved by Fritzing 0.9.3b)
circuit board: 6.3cm x 2.5cm
breadboards: 1

parts:
  IC2 = P82B715PN [chip_label=IC package="DIP (Dual Inline) [THT]"]
  Q1 = HT7333 [part_number=HT7333 package=sot89]
  C1 = Ceramic Capacitor [capacitance=100nF package="100 mil [THT, multilayer]"]
  R1 = Resistor [tolerance=±5% resistance=220 package=THT]
  R2 = Resistor [tolerance=±5% resistance=220 package=THT]
  JIO = female pin header, 10 pins [form="♀ (female)"]
  R3 = Resistor [tolerance=±5% resistance=220 package=THT]
  R4 = Bussed8 Resistor-8 (SIP-9) [tolerance=±5% resistance=10000 package=SIP-9]
  R5 = Resistor [tolerance=±5% resistance=2.2k package=THT]
  R6 = Resistor [tolerance=±5% resistance=2.2k package=THT]
  R7 = Resistor [tolerance=±5% resistance=2.2k package=THT]
  JA = double row male pin header, 6 pins [form="♂ (male)"]
  JI2CB1 = male pin header, 4 pins [form="♂ (male)"]
  JI2CB2 = male pin header, 4 pins [form="♂ (male)"]
  JI2C = male pin header, 4 pins [form="♂ (male)"]
  C2 = Electrolytic Capacitor [capacitance=0.1mF package="100 mil [THT, electrolytic]"]
  C3 = Electrolytic Capacitor [capacitance=10µF package="100 mil [THT, electrolytic]"]
  IC3 = Microchip MCP23008 8-bit I/O expander [part_number=MCP23008 package="DIP (Dual Inline) [THT]"]

nets:
  SCLB: IC2.pin2, JI2CB1.pin3, JI2CB2.pin3
  SCL: IC2.pin3, R2.Pin_1, JI2C.pin3, IC3.SCL
  GND: IC2.pin4, Q1.GND, C1.0, JIO.pin2, R5.Pin_1, R6.Pin_1, R7.Pin_1, JI2CB1.pin1, JI2CB2.pin1, JI2C.pin1, C2.-, C3.-, IC3.VSS
  SDA: IC2.pin6, R1.Pin_1, JI2C.pin2, IC3.SDA
  SDAB: IC2.pin7, JI2CB1.pin2, JI2CB2.pin2
  3.3V: IC2.pin8, Q1.Vout, C1.1, R1.Pin_0, R2.Pin_0, C3.+
  5V: Q1.Vin, JIO.pin1, R3.Pin_1, R4.Pin_0, JA.pin1, JA.pin2, JA.pin3, JI2CB1.pin4, JI2CB2.pin4, JI2C.pin4, C2.+, IC3.VDD
  GIO0: JIO.pin3, R4.Pin_1, IC3.GP0
  GIO1: JIO.pin4, R4.Pin_2, IC3.GP1
  GIO2: JIO.pin5, R4.Pin_3, IC3.GP2
  GIO3: JIO.pin6, R4.Pin_4, IC3.GP3
  GIO4: JIO.pin7, R4.Pin_5, IC3.GP4
  GIO5: JIO.pin8, R4.Pin_6, IC3.GP5
  GIO6: JIO.pin9, R4.Pin_7, IC3.GP6
  GIO7: JIO.pin10, R4.Pin_8, IC3.GP7
  N1: R3.Pin_0, IC3.Reset
  N2: R5.Pin_0, JA.pin6, IC3.A2
  N3: R6.Pin_0, JA.pin5, IC3.A1
  N4: R7.Pin_0, JA.pin4, IC3.A0

notes:
  +5 GND IO0 ... IO7
  GND SDA SCL +5V
  GND LSDA LSCL +5V
  BinkyNet I/O Small 0.0.1
  A0 A1 A2

custom parts:
  P82B715PN: I2C-bus extender
  HT7333: 3v3 regulator
  Bussed8 Resistor-8 (SIP-9): A resistor array is a single package which contains more than one resistor. They are typically used for convenience when several resistors are needed together in the same place in a circuit.
  Microchip MCP23008 8-bit I/O expander: Provides 8-bit, general purpose, parallel I/O expansion for I2C bus. Datasheet: http://ww1.microchip.com/downloads/en/devicedoc/21919e.pdf
