# Fritzing sketch RPiConnector-v1.1 (saved by Fritzing 0.9.3b)
circuit board: 5.24083cm x 1.88096cm
breadboards: 1

parts:
  IC1 = P82B715PN [chip_label="IC " part_number=P82B715 package="DIP (Dual Inline) [THT]"]
  C1 = Ceramic Capacitor [capacitance=100nF package="100 mil [THT, multilayer]"]
  R1 = Resistor [tolerance=±5% resistance=220 package=THT]
  R2 = Resistor [tolerance=±5% resistance=220 package=THT]
  J2 = female pin header, 4 pins [form="♀ (female)"]
  R3 = Resistor [tolerance=±5% resistance=220 package=THT]
  R4 = Resistor [tolerance=±5% resistance=220 package=THT]
  LED2 = LED - 3mm [color="Red (633nm)" package="3 mm [THT]"]
  LED1 = LED - 3mm [color="Green (570nm)" package="3 mm [THT]"]
  RPi_Connector_v1_1 = double row male pin header, 20 pins [form="♂ (male)"]
  J3 = Screw terminal - 2 pins [package=THT]
  Fuse1 = Resettable fuse - PFRA 50

nets:
  N1: IC1.pin2, R2.Pin_0, J2.pin2
  N2: IC1.pin3, RPi_Connector_v1_1.pin3
  GND: IC1.pin4, C1.1, J2.pin4, RPi_Connector_v1_1.pin18, J3.pin2
  N3: IC1.pin6, RPi_Connector_v1_1.pin2
  N4: IC1.pin7, R1.Pin_0, J2.pin3
  N5: IC1.pin8, C1.0, R1.Pin_1, R2.Pin_1, R3.Pin_0, R4.Pin_0, RPi_Connector_v1_1.pin1, RPi_Connector_v1_1.pin9
  N6: J2.pin1, RPi_Connector_v1_1.pin20, Fuse1.A
  N7: R3.Pin_1, LED1.anode
  N8: R4.Pin_1, LED2.anode
  N9: LED2.cathode, RPi_Connector_v1_1.pin12
  N10: LED1.cathode, RPi_Connector_v1_1.pin13
  5V: J3.pin1, Fuse1.B

notes:
  +5V
  gnd
  sda
  scl
  +5 GND

custom parts:
  P82B715PN: I2C-bus extender
  Resettable fuse - PFRA 50: Resettable fuse 0.5A
