# Fritzing sketch RPiConnector (saved by Fritzing 0.9.3b)
circuit board: 5.24083cm x 1.88096cm
breadboards: 1

parts:
  IC1 = P82B715PN [chip_label=IC package="DIP (Dual Inline) [THT]"]
  C1 = Ceramic Capacitor [capacitance=100nF package="100 mil [THT, multilayer]"]
  R1 = Resistor [tolerance=±5% resistance=220 package=THT]
  R2 = Resistor [tolerance=±5% resistance=220 package=THT]
  J2 = female pin header, 4 pins [form="♀ (female)"]
  RPi_Connector_v0_1 = Raspberry Pi Header 40pin [form="♂ (male)" package=THT]
  R3 = Resistor [tolerance=±5% resistance=220 package=THT]
  R4 = Resistor [tolerance=±5% resistance=220 package=THT]
  LED2 = LED - 3mm [color="Red (633nm)" package="3 mm [THT]"]
  LED1 = LED - 3mm [color="Green (570nm)" package="3 mm [THT]"]

nets:
  N1: IC1.pin2, R2.Pin_0, J2.pin2
  N2: IC1.pin3, RPi_Connector_v0_1.GPIO3
  N3: IC1.pin4, C1.1, J2.pin4, RPi_Connector_v0_1.GND
  N4: IC1.pin6, RPi_Connector_v0_1.GPIO2
  N5: IC1.pin7, R1.Pin_0, J2.pin3
  3V3: IC1.pin8, C1.0, R1.Pin_1, R2.Pin_1, RPi_Connector_v0_1.3v3, RPi_Connector_v0_1.3V3, R3.Pin_0, R4.Pin_0
  N6: J2.pin1, RPi_Connector_v0_1.5V
  N7: RPi_Connector_v0_1.GIPO24, LED2.cathode
  N8: RPi_Connector_v0_1.GIPO23, LED1.cathode
  N9: R3.Pin_1, LED1.anode
  N10: R4.Pin_1, LED2.anode

notes:
  +5V
  gnd
  sda
  scl

custom parts:
  P82B715PN: I2C-bus extender
  Raspberry Pi Header 40pin: Raspberry Pi 40 pin header - for creating your own shields.
